// Logisim project PROJECT_X8.circ as structural Verilog: 13 circuits, main circuit main
module main (
);

  Ram512byte ram512byte_1 ();  // open: We, Re, F, A0, A1, A2, A3, A4, A5, A6, A7, B0, B1, B2, B3, B4, B5, B6, B7, T0, T1, T2, T3, T4, T5, T6, T7
endmodule

module f_1bit_adder (
  input  a,
  input  b,
  input  o_c,
  output s,
  output c
);

  wire and_1_out, and_2_out, xor_1_out;

  xor xor_1 (xor_1_out, a, b);
  and and_1 (and_1_out, a, b);
  and and_2 (and_2_out, xor_1_out, o_c);
  xor xor_2 (s, a, b, o_c);
  or or_1 (c, and_1_out, and_2_out);
endmodule

module I8bit_adder (
  input  a7,
  input  a6,
  input  a5,
  input  a4,
  input  a3,
  input  a2,
  input  a1,
  input  a0,
  input  b7,
  input  b6,
  input  b5,
  input  b4,
  input  b3,
  input  b2,
  input  b1,
  input  b0,
  input  o_c,
  output c,
  output s7,
  output s6,
  output s5,
  output s4,
  output s3,
  output s2,
  output s1,
  output s0
);

  wire f_1bit_adder_2_c, f_1bit_adder_3_c, f_1bit_adder_4_c, f_1bit_adder_5_c, f_1bit_adder_6_c,
       f_1bit_adder_7_c, f_1bit_adder_8_c;

  f_1bit_adder f_1bit_adder_1 (.a(a7), .b(b7), .o_c(f_1bit_adder_2_c), .s(s7), .c(c));
  f_1bit_adder f_1bit_adder_2 (.a(a6), .b(b6), .o_c(f_1bit_adder_3_c), .s(s6), .c(f_1bit_adder_2_c));
  f_1bit_adder f_1bit_adder_3 (.a(a5), .b(b5), .o_c(f_1bit_adder_4_c), .s(s5), .c(f_1bit_adder_3_c));
  f_1bit_adder f_1bit_adder_4 (.a(a4), .b(b4), .o_c(f_1bit_adder_5_c), .s(s4), .c(f_1bit_adder_4_c));
  f_1bit_adder f_1bit_adder_5 (.a(a3), .b(b3), .o_c(f_1bit_adder_6_c), .s(s3), .c(f_1bit_adder_5_c));
  f_1bit_adder f_1bit_adder_6 (.a(a2), .b(b2), .o_c(f_1bit_adder_7_c), .s(s2), .c(f_1bit_adder_6_c));
  f_1bit_adder f_1bit_adder_7 (.a(a1), .b(b1), .o_c(f_1bit_adder_8_c), .s(s1), .c(f_1bit_adder_7_c));
  f_1bit_adder f_1bit_adder_8 (.a(a0), .b(b0), .o_c(o_c), .s(s0), .c(f_1bit_adder_8_c));
endmodule

module I8bit_subs (
  input  a7,
  input  a6,
  input  a5,
  input  a4,
  input  a3,
  input  a2,
  input  a1,
  input  a0,
  input  b7,
  input  b6,
  input  b5,
  input  b4,
  input  b3,
  input  b2,
  input  b1,
  input  b0,
  input  flag,
  input  CinS,
  input  CinA,
  output CoutA,
  output s7,
  output s6,
  output s5,
  output s4,
  output s3,
  output s2,
  output s1,
  output s0,
  output CoutS
);

  wire i8bit_adder_1_s0, i8bit_adder_1_s1, i8bit_adder_1_s2, i8bit_adder_1_s3, i8bit_adder_1_s4,
       i8bit_adder_1_s5, i8bit_adder_1_s6, i8bit_adder_1_s7, not_1_out, not_2_out, not_3_out, not_4_out,
       not_5_out, not_6_out, not_7_out, not_8_out;

  not not_1 (not_1_out, b7);
  not not_2 (not_2_out, b6);
  not not_3 (not_3_out, b5);
  not not_4 (not_4_out, b4);
  not not_5 (not_5_out, b3);
  not not_6 (not_6_out, b2);
  not not_7 (not_7_out, b1);
  not not_8 (not_8_out, b0);
  I8bit_adder i8bit_adder_1 (
    .a7(not_1_out), .a6(not_2_out), .a5(not_3_out), .a4(not_4_out), .a3(not_5_out), .a2(not_6_out),
    .a1(not_7_out), .a0(not_8_out), .b7(1'b0), .b6(1'b0), .b5(1'b0), .b4(1'b0), .b3(1'b0), .b2(1'b0),
    .b1(1'b0), .b0(flag), .o_c(CinS), .c(CoutS), .s7(i8bit_adder_1_s7), .s6(i8bit_adder_1_s6),
    .s5(i8bit_adder_1_s5), .s4(i8bit_adder_1_s4), .s3(i8bit_adder_1_s3), .s2(i8bit_adder_1_s2),
    .s1(i8bit_adder_1_s1), .s0(i8bit_adder_1_s0));
  I8bit_adder i8bit_adder_2 (
    .a7(a7), .a6(a6), .a5(a5), .a4(a4), .a3(a3), .a2(a2), .a1(a1), .a0(a0), .b7(i8bit_adder_1_s7),
    .b6(i8bit_adder_1_s6), .b5(i8bit_adder_1_s5), .b4(i8bit_adder_1_s4), .b3(i8bit_adder_1_s3),
    .b2(i8bit_adder_1_s2), .b1(i8bit_adder_1_s1), .b0(i8bit_adder_1_s0), .o_c(CinA), .c(CoutA), .s7(s7),
    .s6(s6), .s5(s5), .s4(s4), .s3(s3), .s2(s2), .s1(s1), .s0(s0));
endmodule

module SreL (
  input  \bit ,
  input  We,
  input  Re,
  output R
);

  wire and_1_out, and_2_out, and_3_out, and_4_out, not_1_out, not_2_out, or_1_out;

  not not_1 (not_1_out, \bit );
  and and_1 (and_1_out, not_1_out, We);
  and and_2 (and_2_out, \bit , We);
  not not_2 (not_2_out, and_1_out);
  and and_3 (and_3_out, not_2_out, and_2_out);
  and and_4 (and_4_out, or_1_out, not_2_out);
  or or_1 (or_1_out, and_3_out, and_4_out);
  and and_5 (R, or_1_out, Re);
endmodule

module I8bit_register (
  input  We,
  input  Re,
  input  b7,
  input  b6,
  input  b5,
  input  b4,
  input  b3,
  input  b2,
  input  b1,
  input  b0,
  output T7,
  output T6,
  output T5,
  output T4,
  output T3,
  output T2,
  output T1,
  output T0
);

  SreL srel_1 (.\bit (b7), .We(We), .Re(Re), .R(T7));
  SreL srel_2 (.\bit (b6), .We(We), .Re(Re), .R(T6));
  SreL srel_3 (.\bit (b5), .We(We), .Re(Re), .R(T5));
  SreL srel_4 (.\bit (b4), .We(We), .Re(Re), .R(T4));
  SreL srel_5 (.\bit (b3), .We(We), .Re(Re), .R(T3));
  SreL srel_6 (.\bit (b2), .We(We), .Re(Re), .R(T2));
  SreL srel_7 (.\bit (b1), .We(We), .Re(Re), .R(T1));
  SreL srel_8 (.\bit (b0), .We(We), .Re(Re), .R(T0));
endmodule

module C416 (
  input  In0,
  input  In1,
  input  In2,
  input  In3,
  output T0,
  output T1,
  output T2,
  output T3,
  output T4,
  output T5,
  output T6,
  output T7,
  output T8,
  output T9,
  output T10,
  output T11,
  output T12,
  output T13,
  output T14,
  output T15
);

  wire not_1_out, not_2_out, not_3_out, not_4_out, not_5_out, not_6_out, not_7_out, not_8_out, not_9_out,
       not_10_out, not_11_out, not_12_out, not_13_out, not_14_out, not_15_out, not_16_out, not_17_out,
       not_18_out, not_19_out, not_20_out, not_21_out, not_22_out, not_23_out, not_24_out, not_25_out,
       not_26_out, not_27_out, not_28_out, not_29_out, not_30_out, not_31_out, not_32_out;

  not not_1 (not_1_out, In0);
  not not_2 (not_2_out, In1);
  not not_3 (not_3_out, In2);
  not not_4 (not_4_out, In3);
  not not_5 (not_5_out, In1);
  not not_6 (not_6_out, In2);
  not not_7 (not_7_out, In3);
  not not_8 (not_8_out, In0);
  not not_9 (not_9_out, In2);
  not not_10 (not_10_out, In3);
  not not_11 (not_11_out, In2);
  not not_12 (not_12_out, In3);
  not not_13 (not_13_out, In0);
  not not_14 (not_14_out, In1);
  not not_15 (not_15_out, In3);
  not not_16 (not_16_out, In1);
  not not_17 (not_17_out, In3);
  not not_18 (not_18_out, In0);
  not not_19 (not_19_out, In3);
  not not_20 (not_20_out, In3);
  not not_21 (not_21_out, In0);
  not not_22 (not_22_out, In1);
  not not_23 (not_23_out, In2);
  not not_24 (not_24_out, In1);
  not not_25 (not_25_out, In2);
  not not_26 (not_26_out, In0);
  not not_27 (not_27_out, In2);
  not not_28 (not_28_out, In2);
  not not_29 (not_29_out, In0);
  not not_30 (not_30_out, In1);
  not not_31 (not_31_out, In1);
  not not_32 (not_32_out, In0);
  and and_1 (T0, not_1_out, not_2_out, not_3_out, not_4_out);
  and and_2 (T1, In0, not_5_out, not_6_out, not_7_out);
  and and_3 (T2, not_8_out, In1, not_9_out, not_10_out);
  and and_4 (T3, In0, In1, not_11_out, not_12_out);
  and and_5 (T4, not_13_out, not_14_out, In2, not_15_out);
  and and_6 (T5, In0, not_16_out, In2, not_17_out);
  and and_7 (T6, not_18_out, In1, In2, not_19_out);
  and and_8 (T7, In0, In1, In2, not_20_out);
  and and_9 (T8, not_21_out, not_22_out, not_23_out, In3);
  and and_10 (T9, In0, not_24_out, not_25_out, In3);
  and and_11 (T10, not_26_out, In1, not_27_out, In3);
  and and_12 (T11, In0, In1, not_28_out, In3);
  and and_13 (T12, not_29_out, not_30_out, In2, In3);
  and and_14 (T13, In0, not_31_out, In2, In3);
  and and_15 (T14, not_32_out, In1, In2, In3);
  and and_16 (T15, In0, In1, In2, In3);
endmodule

module The16bit (
  input  A0,
  input  A1,
  input  A2,
  input  A3,
  input  Re,
  input  B,
  input  We,
  input  Flag,
  output T
);

  wire and_1_out, and_2_out, and_3_out, c24_1_t0, c24_1_t1, c24_1_t2, c24_1_t3, c24_2_t0, c24_2_t1, c24_2_t2,
       c24_2_t3, or_2_out, or_3_out, or_4_out, or_5_out, or_6_out, or_7_out, or_8_out, or_9_out, or_10_out,
       or_11_out, or_12_out, or_13_out, srelforram_1_t, srelforram_2_t, srelforram_3_t, srelforram_4_t,
       srelforram_5_t, srelforram_6_t, srelforram_7_t, srelforram_8_t, srelforram_9_t, srelforram_10_t,
       srelforram_11_t, srelforram_12_t, srelforram_13_t, srelforram_14_t, srelforram_15_t, srelforram_16_t;

  C24 c24_1 (.B0(A2), .B1(A3), .T0(c24_1_t0), .T1(c24_1_t1), .T2(c24_1_t2), .T3(c24_1_t3));
  or or_1 (T, or_2_out, or_3_out, or_4_out, or_5_out);
  and and_1 (and_1_out, Re, Flag);
  and and_2 (and_2_out, B, Flag);
  and and_3 (and_3_out, We, Flag);
  SrelForRam srelforram_1 (
    .T(srelforram_1_t), .We(and_3_out), .C(c24_2_t0), .R(c24_1_t0), .Re(and_1_out), .B(and_2_out));
  SrelForRam srelforram_2 (
    .T(srelforram_2_t), .We(and_3_out), .C(c24_2_t0), .R(c24_1_t1), .Re(and_1_out), .B(and_2_out));
  SrelForRam srelforram_3 (
    .T(srelforram_3_t), .We(and_3_out), .C(c24_2_t0), .R(c24_1_t2), .Re(and_1_out), .B(and_2_out));
  SrelForRam srelforram_4 (
    .T(srelforram_4_t), .We(and_3_out), .C(c24_2_t0), .R(c24_1_t3), .Re(and_1_out), .B(and_2_out));
  or or_2 (or_2_out, srelforram_1_t, or_6_out);
  or or_3 (or_3_out, srelforram_2_t, or_7_out);
  or or_4 (or_4_out, srelforram_3_t, or_8_out);
  or or_5 (or_5_out, srelforram_4_t, or_9_out);
  C24 c24_2 (.B0(A0), .B1(A1), .T0(c24_2_t0), .T1(c24_2_t1), .T2(c24_2_t2), .T3(c24_2_t3));
  SrelForRam srelforram_5 (
    .T(srelforram_5_t), .We(and_3_out), .C(c24_2_t1), .R(c24_1_t0), .Re(and_1_out), .B(and_2_out));
  SrelForRam srelforram_6 (
    .T(srelforram_6_t), .We(and_3_out), .C(c24_2_t1), .R(c24_1_t1), .Re(and_1_out), .B(and_2_out));
  SrelForRam srelforram_7 (
    .T(srelforram_7_t), .We(and_3_out), .C(c24_2_t1), .R(c24_1_t2), .Re(and_1_out), .B(and_2_out));
  SrelForRam srelforram_8 (
    .T(srelforram_8_t), .We(and_3_out), .C(c24_2_t1), .R(c24_1_t3), .Re(and_1_out), .B(and_2_out));
  or or_6 (or_6_out, srelforram_5_t, or_10_out);
  or or_7 (or_7_out, srelforram_6_t, or_11_out);
  or or_8 (or_8_out, srelforram_7_t, or_12_out);
  or or_9 (or_9_out, srelforram_8_t, or_13_out);
  SrelForRam srelforram_9 (
    .T(srelforram_9_t), .We(and_3_out), .C(c24_2_t2), .R(c24_1_t0), .Re(and_1_out), .B(and_2_out));
  SrelForRam srelforram_10 (
    .T(srelforram_10_t), .We(and_3_out), .C(c24_2_t2), .R(c24_1_t1), .Re(and_1_out), .B(and_2_out));
  SrelForRam srelforram_11 (
    .T(srelforram_11_t), .We(and_3_out), .C(c24_2_t2), .R(c24_1_t2), .Re(and_1_out), .B(and_2_out));
  SrelForRam srelforram_12 (
    .T(srelforram_12_t), .We(and_3_out), .C(c24_2_t2), .R(c24_1_t3), .Re(and_1_out), .B(and_2_out));
  or or_10 (or_10_out, srelforram_9_t, srelforram_13_t);
  or or_11 (or_11_out, srelforram_10_t, srelforram_14_t);
  or or_12 (or_12_out, srelforram_11_t, srelforram_15_t);
  or or_13 (or_13_out, srelforram_12_t, srelforram_16_t);
  SrelForRam srelforram_13 (
    .T(srelforram_13_t), .We(and_3_out), .C(c24_2_t3), .R(c24_1_t0), .Re(and_1_out), .B(and_2_out));
  SrelForRam srelforram_14 (
    .T(srelforram_14_t), .We(and_3_out), .C(c24_2_t3), .R(c24_1_t1), .Re(and_1_out), .B(and_2_out));
  SrelForRam srelforram_15 (
    .T(srelforram_15_t), .We(and_3_out), .C(c24_2_t3), .R(c24_1_t2), .Re(and_1_out), .B(and_2_out));
  SrelForRam srelforram_16 (
    .T(srelforram_16_t), .We(and_3_out), .C(c24_2_t3), .R(c24_1_t3), .Re(and_1_out), .B(and_2_out));

  // Other names for the same wires on the sheet: L = Flag
endmodule

module SrelForRam (
  input  B,
  input  We,
  input  C,
  input  R,
  input  Re,
  output T
);

  wire and_1_out, and_2_out;

  and and_1 (and_1_out, We, R, C);
  and and_2 (and_2_out, C, Re, R);
  SreL srel_1 (.\bit (B), .We(and_1_out), .Re(and_2_out), .R(T));
endmodule

module C24 (
  input  B0,
  input  B1,
  output T0,
  output T1,
  output T2,
  output T3
);

  wire not_1_out, not_2_out, not_3_out, not_4_out;

  not not_1 (not_1_out, B0);
  not not_2 (not_2_out, B1);
  not not_3 (not_3_out, B1);
  not not_4 (not_4_out, B0);
  and and_1 (T0, not_1_out, not_2_out);
  and and_2 (T1, B0, not_3_out);
  and and_3 (T2, not_4_out, B1);
  and and_4 (T3, B0, B0);
endmodule

module Ram256Bit (
  input  A0,
  input  A1,
  input  A2,
  input  A3,
  input  RE,
  input  B,
  input  We,
  input  A4,
  input  A5,
  input  A6,
  input  A7,
  output T
);

  wire c416_1_t0, c416_1_t1, c416_1_t2, c416_1_t3, c416_1_t4, c416_1_t5, c416_1_t6, c416_1_t7, c416_1_t8,
       c416_1_t9, c416_1_t10, c416_1_t11, c416_1_t12, c416_1_t13, c416_1_t14, c416_1_t15, or_1_out, or_2_out,
       or_3_out, or_4_out, or_5_out, or_6_out, or_7_out, or_9_out, or_10_out, or_11_out, or_12_out,
       or_13_out, or_14_out, or_15_out, the16bit_1_t, the16bit_2_t, the16bit_3_t, the16bit_4_t, the16bit_5_t,
       the16bit_6_t, the16bit_7_t, the16bit_8_t, the16bit_9_t, the16bit_10_t, the16bit_11_t, the16bit_12_t,
       the16bit_13_t, the16bit_14_t, the16bit_15_t, the16bit_16_t;

  C416 c416_1 (
    .In0(A4), .In1(A5), .In2(A6), .In3(A7), .T0(c416_1_t0), .T1(c416_1_t1), .T2(c416_1_t2), .T3(c416_1_t3),
    .T4(c416_1_t4), .T5(c416_1_t5), .T6(c416_1_t6), .T7(c416_1_t7), .T8(c416_1_t8), .T9(c416_1_t9),
    .T10(c416_1_t10), .T11(c416_1_t11), .T12(c416_1_t12), .T13(c416_1_t13), .T14(c416_1_t14), .T15(c416_1_t15));
  The16bit the16bit_1 (.T(the16bit_1_t), .A0(A0), .A1(A1), .A2(A2), .A3(A3), .Flag(c416_1_t0), .Re(RE), .B(B), .We(We));
  The16bit the16bit_2 (.T(the16bit_2_t), .A0(A0), .A1(A1), .A2(A2), .A3(A3), .Flag(c416_1_t1), .Re(RE), .B(B), .We(We));
  The16bit the16bit_3 (.T(the16bit_3_t), .A0(A0), .A1(A1), .A2(A2), .A3(A3), .Flag(c416_1_t2), .Re(RE), .B(B), .We(We));
  The16bit the16bit_4 (.T(the16bit_4_t), .A0(A0), .A1(A1), .A2(A2), .A3(A3), .Flag(c416_1_t3), .Re(RE), .B(B), .We(We));
  The16bit the16bit_5 (.T(the16bit_5_t), .A0(A0), .A1(A1), .A2(A2), .A3(A3), .Flag(c416_1_t4), .Re(RE), .B(B), .We(We));
  The16bit the16bit_6 (.T(the16bit_6_t), .A0(A0), .A1(A1), .A2(A2), .A3(A3), .Flag(c416_1_t5), .Re(RE), .B(B), .We(We));
  The16bit the16bit_7 (.T(the16bit_7_t), .A0(A0), .A1(A1), .A2(A2), .A3(A3), .Flag(c416_1_t6), .Re(RE), .B(B), .We(We));
  The16bit the16bit_8 (.T(the16bit_8_t), .A0(A0), .A1(A1), .A2(A2), .A3(A3), .Flag(c416_1_t7), .Re(RE), .B(B), .We(We));
  or or_1 (or_1_out, the16bit_1_t, or_2_out);
  or or_2 (or_2_out, the16bit_2_t, or_3_out);
  or or_3 (or_3_out, the16bit_3_t, or_4_out);
  or or_4 (or_4_out, the16bit_4_t, or_5_out);
  or or_5 (or_5_out, the16bit_5_t, or_6_out);
  or or_6 (or_6_out, the16bit_6_t, or_7_out);
  or or_7 (or_7_out, the16bit_7_t, the16bit_8_t);
  The16bit the16bit_9 (.T(the16bit_9_t), .A0(A0), .A1(A1), .A2(A2), .A3(A3), .Flag(c416_1_t8), .Re(RE), .B(B), .We(We));
  The16bit the16bit_10 (
    .T(the16bit_10_t), .A0(A0), .A1(A1), .A2(A2), .A3(A3), .Flag(c416_1_t9), .Re(RE), .B(B), .We(We));
  The16bit the16bit_11 (
    .T(the16bit_11_t), .A0(A0), .A1(A1), .A2(A2), .A3(A3), .Flag(c416_1_t10), .Re(RE), .B(B), .We(We));
  The16bit the16bit_12 (
    .T(the16bit_12_t), .A0(A0), .A1(A1), .A2(A2), .A3(A3), .Flag(c416_1_t11), .Re(RE), .B(B), .We(We));
  The16bit the16bit_13 (
    .T(the16bit_13_t), .A0(A0), .A1(A1), .A2(A2), .A3(A3), .Flag(c416_1_t12), .Re(RE), .B(B), .We(We));
  The16bit the16bit_14 (
    .T(the16bit_14_t), .A0(A0), .A1(A1), .A2(A2), .A3(A3), .Flag(c416_1_t13), .Re(RE), .B(B), .We(We));
  The16bit the16bit_15 (
    .T(the16bit_15_t), .A0(A0), .A1(A1), .A2(A2), .A3(A3), .Flag(c416_1_t14), .Re(RE), .B(B), .We(We));
  The16bit the16bit_16 (
    .T(the16bit_16_t), .A0(A0), .A1(A1), .A2(A2), .A3(A3), .Flag(c416_1_t15), .Re(RE), .B(B), .We(We));
  or or_8 (T, or_1_out, or_9_out);
  or or_9 (or_9_out, the16bit_9_t, or_10_out);
  or or_10 (or_10_out, the16bit_10_t, or_11_out);
  or or_11 (or_11_out, the16bit_11_t, or_12_out);
  or or_12 (or_12_out, the16bit_12_t, or_13_out);
  or or_13 (or_13_out, the16bit_13_t, or_14_out);
  or or_14 (or_14_out, the16bit_14_t, or_15_out);
  or or_15 (or_15_out, the16bit_15_t, the16bit_16_t);
endmodule

module Ram256Byte (
  input  A0,
  input  A1,
  input  A2,
  input  A3,
  input  Re,
  input  We,
  input  A4,
  input  A5,
  input  A6,
  input  A7,
  input  B0,
  input  B1,
  input  B2,
  input  B3,
  input  B4,
  input  B5,
  input  B6,
  input  B7,
  output T0,
  output T1,
  output T2,
  output T3,
  output T4,
  output T5,
  output T6,
  output T7
);

  Ram256Bit ram256bit_1 (
    .A0(A0), .A1(A1), .A2(A2), .A3(A3), .RE(Re), .B(B0), .We(We), .A4(A4), .A5(A5), .A6(A6), .A7(A7), .T(T0));
  Ram256Bit ram256bit_2 (
    .A0(A0), .A1(A1), .A2(A2), .A3(A3), .RE(Re), .B(B1), .We(We), .A4(A4), .A5(A5), .A6(A6), .A7(A7), .T(T1));
  Ram256Bit ram256bit_3 (
    .A0(A0), .A1(A1), .A2(A2), .A3(A3), .RE(Re), .B(B2), .We(We), .A4(A4), .A5(A5), .A6(A6), .A7(A7), .T(T2));
  Ram256Bit ram256bit_4 (
    .A0(A0), .A1(A1), .A2(A2), .A3(A3), .RE(Re), .B(B3), .We(We), .A4(A4), .A5(A5), .A6(A6), .A7(A7), .T(T3));
  Ram256Bit ram256bit_5 (
    .A0(A0), .A1(A1), .A2(A2), .A3(A3), .RE(Re), .B(B4), .We(We), .A4(A4), .A5(A5), .A6(A6), .A7(A7), .T(T4));
  Ram256Bit ram256bit_6 (
    .A0(A0), .A1(A1), .A2(A2), .A3(A3), .RE(Re), .B(B5), .We(We), .A4(A4), .A5(A5), .A6(A6), .A7(A7), .T(T5));
  Ram256Bit ram256bit_7 (
    .A0(A0), .A1(A1), .A2(A2), .A3(A3), .RE(Re), .B(B6), .We(We), .A4(A4), .A5(A5), .A6(A6), .A7(A7), .T(T6));
  Ram256Bit ram256bit_8 (
    .A0(A0), .A1(A1), .A2(A2), .A3(A3), .RE(Re), .B(B7), .We(We), .A4(A4), .A5(A5), .A6(A6), .A7(A7), .T(T7));
endmodule

module Ram512byte (
  input  We,
  input  Re,
  input  F,
  input  A0,
  input  A1,
  input  A2,
  input  A3,
  input  A4,
  input  A5,
  input  A6,
  input  A7,
  input  B0,
  input  B1,
  input  B2,
  input  B3,
  input  B4,
  input  B5,
  input  B6,
  input  B7,
  output T0,
  output T1,
  output T2,
  output T3,
  output T4,
  output T5,
  output T6,
  output T7
);

  wire and_1_out, and_2_out, and_3_out, and_4_out, not_1_out, not_2_out, ram256byte_1_t0, ram256byte_1_t1,
       ram256byte_1_t2, ram256byte_1_t3, ram256byte_1_t4, ram256byte_1_t5, ram256byte_1_t6, ram256byte_1_t7,
       ram256byte_2_t0, ram256byte_2_t1, ram256byte_2_t2, ram256byte_2_t3, ram256byte_2_t4, ram256byte_2_t5,
       ram256byte_2_t6, ram256byte_2_t7;

  not not_1 (not_1_out, F);
  and and_1 (and_1_out, not_1_out, We);
  not not_2 (not_2_out, F);
  and and_2 (and_2_out, not_2_out, Re);
  and and_3 (and_3_out, We, F);
  and and_4 (and_4_out, Re, F);
  Ram256Byte ram256byte_1 (
    .A0(A0), .A1(A1), .A2(A2), .A3(A3), .Re(and_2_out), .We(and_1_out), .A4(A4), .A5(A5), .A6(A6), .A7(A7),
    .B0(B0), .B1(B1), .B2(B2), .B3(B3), .B4(B4), .B5(B5), .B6(B6), .B7(B7), .T0(ram256byte_1_t0),
    .T1(ram256byte_1_t1), .T2(ram256byte_1_t2), .T3(ram256byte_1_t3), .T4(ram256byte_1_t4),
    .T5(ram256byte_1_t5), .T6(ram256byte_1_t6), .T7(ram256byte_1_t7));
  Ram256Byte ram256byte_2 (
    .A0(A0), .A1(A1), .A2(A2), .A3(A3), .Re(and_4_out), .We(and_3_out), .A4(A4), .A5(A5), .A6(A6), .A7(A7),
    .B0(B0), .B1(B1), .B2(B2), .B3(B3), .B4(B4), .B5(B5), .B6(B6), .B7(B7), .T0(ram256byte_2_t0),
    .T1(ram256byte_2_t1), .T2(ram256byte_2_t2), .T3(ram256byte_2_t3), .T4(ram256byte_2_t4),
    .T5(ram256byte_2_t5), .T6(ram256byte_2_t6), .T7(ram256byte_2_t7));
  or or_1 (T0, ram256byte_1_t0, ram256byte_2_t0);
  or or_2 (T1, ram256byte_1_t1, ram256byte_2_t1);
  or or_3 (T2, ram256byte_1_t2, ram256byte_2_t2);
  or or_4 (T3, ram256byte_1_t3, ram256byte_2_t3);
  or or_5 (T4, ram256byte_1_t4, ram256byte_2_t4);
  or or_6 (T5, ram256byte_1_t5, ram256byte_2_t5);
  or or_7 (T6, ram256byte_1_t6, ram256byte_2_t6);
  or or_8 (T7, ram256byte_1_t7, ram256byte_2_t7);
endmodule
