// Logisim project PROJECT_Z.circ as structural Verilog: 3 circuits, main circuit main
module main (
);

  wire dipswitch_1_sw1, dipswitch_1_sw2, dipswitch_1_sw3, dipswitch_1_sw4, dipswitch_1_sw5, dipswitch_1_sw6,
       dipswitch_1_sw7, dipswitch_1_sw8, dipswitch_2_p1, dipswitch_2_p2, dipswitch_2_p3, dipswitch_2_p4,
       dipswitch_2_p5, dipswitch_2_p6, dipswitch_2_p7, dipswitch_2_p8, i8bit_adder_1_c, i8bit_adder_1_s0,
       i8bit_adder_1_s1, i8bit_adder_1_s2, i8bit_adder_1_s3, i8bit_adder_1_s4, i8bit_adder_1_s5,
       i8bit_adder_1_s6, i8bit_adder_1_s7;

  DipSwitch dipswitch_1 (
    .sw1(dipswitch_1_sw1), .sw2(dipswitch_1_sw2), .sw3(dipswitch_1_sw3), .sw4(dipswitch_1_sw4),
    .sw5(dipswitch_1_sw5), .sw6(dipswitch_1_sw6), .sw7(dipswitch_1_sw7), .sw8(dipswitch_1_sw8));
  // DipSwitch dipswitch_2: pin names not known; wires that end beside it: dipswitch_2_p1, dipswitch_2_p2, dipswitch_2_p3, dipswitch_2_p4, dipswitch_2_p5, dipswitch_2_p6, dipswitch_2_p7, dipswitch_2_p8
  I8bit_adder i8bit_adder_1 (
    .a7(dipswitch_2_p8), .a6(dipswitch_2_p7), .a5(dipswitch_2_p6), .a4(dipswitch_2_p5), .a3(dipswitch_2_p4),
    .a2(dipswitch_2_p3), .a1(dipswitch_2_p2), .a0(dipswitch_2_p1), .b7(dipswitch_1_sw8),
    .b6(dipswitch_1_sw7), .b5(dipswitch_1_sw6), .b4(dipswitch_1_sw5), .b3(dipswitch_1_sw4),
    .b2(dipswitch_1_sw3), .b1(dipswitch_1_sw2), .b0(dipswitch_1_sw1), .o_c(1'b0), .c(i8bit_adder_1_c),
    .s7(i8bit_adder_1_s7), .s6(i8bit_adder_1_s6), .s5(i8bit_adder_1_s5), .s4(i8bit_adder_1_s4),
    .s3(i8bit_adder_1_s3), .s2(i8bit_adder_1_s2), .s1(i8bit_adder_1_s1), .s0(i8bit_adder_1_s0));
  LED led_1 (.in(i8bit_adder_1_c));
  LED led_2 (.in(i8bit_adder_1_s7));
  LED led_3 (.in(i8bit_adder_1_s6));
  LED led_4 (.in(i8bit_adder_1_s5));
  LED led_5 (.in(i8bit_adder_1_s4));
  LED led_6 (.in(i8bit_adder_1_s3));
  LED led_7 (.in(i8bit_adder_1_s2));
  LED led_8 (.in(i8bit_adder_1_s1));
  LED led_9 (.in(i8bit_adder_1_s0));
endmodule

module f_1bit_adder (
  input  a,
  input  b,
  input  o_c,
  output s,
  output c
);

  wire and_1_out, and_2_out, xor_1_out;

  xor xor_1 (xor_1_out, a, b);
  and and_1 (and_1_out, a, b);
  and and_2 (and_2_out, xor_1_out, o_c);
  xor xor_2 (s, a, b, o_c);
  or or_1 (c, and_1_out, and_2_out);
endmodule

module I8bit_adder (
  input  a7,
  input  a6,
  input  a5,
  input  a4,
  input  a3,
  input  a2,
  input  a1,
  input  a0,
  input  b7,
  input  b6,
  input  b5,
  input  b4,
  input  b3,
  input  b2,
  input  b1,
  input  b0,
  input  o_c,
  output c,
  output s7,
  output s6,
  output s5,
  output s4,
  output s3,
  output s2,
  output s1,
  output s0
);

  wire f_1bit_adder_2_c, f_1bit_adder_3_c, f_1bit_adder_4_c, f_1bit_adder_5_c, f_1bit_adder_6_c,
       f_1bit_adder_7_c, f_1bit_adder_8_c;

  f_1bit_adder f_1bit_adder_1 (.a(a7), .b(b7), .o_c(f_1bit_adder_2_c), .s(s7), .c(c));
  f_1bit_adder f_1bit_adder_2 (.a(a6), .b(b6), .o_c(f_1bit_adder_3_c), .s(s6), .c(f_1bit_adder_2_c));
  f_1bit_adder f_1bit_adder_3 (.a(a5), .b(b5), .o_c(f_1bit_adder_4_c), .s(s5), .c(f_1bit_adder_3_c));
  f_1bit_adder f_1bit_adder_4 (.a(a4), .b(b4), .o_c(f_1bit_adder_5_c), .s(s4), .c(f_1bit_adder_4_c));
  f_1bit_adder f_1bit_adder_5 (.a(a3), .b(b3), .o_c(f_1bit_adder_6_c), .s(s3), .c(f_1bit_adder_5_c));
  f_1bit_adder f_1bit_adder_6 (.a(a2), .b(b2), .o_c(f_1bit_adder_7_c), .s(s2), .c(f_1bit_adder_6_c));
  f_1bit_adder f_1bit_adder_7 (.a(a1), .b(b1), .o_c(f_1bit_adder_8_c), .s(s1), .c(f_1bit_adder_7_c));
  f_1bit_adder f_1bit_adder_8 (.a(a0), .b(b0), .o_c(o_c), .s(s0), .c(f_1bit_adder_8_c));
endmodule
